# Fritzing sketch puertadesalida (saved by Fritzing 0.9.2b)
breadboards: 1

parts:
  Parte1 = Arduino Uno (Rev3)
  S1 = Pushbutton [package="[THT]"]
  S2 = Pushbutton [package="[THT]"]
  S3 = Pushbutton [package="[THT]"]
  S4 = Pushbutton [package="[THT]"]
  S5 = Pushbutton [package="[THT]"]
  S6 = Pushbutton [package="[THT]"]
  S7 = Pushbutton [package="[THT]"]
  S8 = Pushbutton [package="[THT]"]
  R1 = Resistor [tolerance=±5% resistance=220 package=THT]
  R2 = Resistor [tolerance=±5% resistance=220 package=THT]
  R3 = Resistor [tolerance=±5% resistance=220 package=THT]
  R4 = Resistor [tolerance=±5% resistance=220 package=THT]
  R5 = Resistor [tolerance=±5% resistance=220 package=THT]
  R6 = Resistor [tolerance=±5% resistance=220 package=THT]
  R7 = Resistor [tolerance=±5% resistance=220 package=THT]
  R8 = Resistor [tolerance=±5% resistance=220 package=THT]
  LED1 = LED - 5mm [color="Red (633nm)" package="5 mm [THT]"]
  LED2 = LED - 5mm [color="Red (633nm)" package="5 mm [THT]"]

nets:
  N1: Parte1.D8, S3.Pin_3, S3.Pin_4, R3.Pin_0
  N2: Parte1.D9_PWM, S2.Pin_3, S2.Pin_4, R2.Pin_0
  N3: Parte1.D10_PWM/SS, S1.Pin_3, S1.Pin_4, R1.Pin_0
  N4: Parte1.D13/SCK, LED2.cathode
  N5: Parte1.GND, R1.Pin_1, R2.Pin_1, R3.Pin_1, R4.Pin_1, R5.Pin_1, R6.Pin_1, R7.Pin_1, R8.Pin_1, LED1.anode, LED2.anode
  N6: Parte1.D2, LED1.cathode
  N7: Parte1.D3_PWM, S8.Pin_3, S8.Pin_4, R8.Pin_0
  N8: Parte1.D4, S7.Pin_3, S7.Pin_4, R7.Pin_0
  N9: Parte1.D5_PWM, S6.Pin_3, S6.Pin_4, R6.Pin_0
  N10: Parte1.D6_PWM, S5.Pin_3, S5.Pin_4, R5.Pin_0
  N11: Parte1.D7, S4.Pin_3, S4.Pin_4, R4.Pin_0
  N12: Parte1.5V, S1.Pin_1, S1.Pin_2, S2.Pin_1, S2.Pin_2, S3.Pin_1, S3.Pin_2, S4.Pin_1, S4.Pin_2, S5.Pin_1, S5.Pin_2, S6.Pin_1, S6.Pin_2, S7.Pin_1, S7.Pin_2, S8.Pin_1, S8.Pin_2
