# Fritzing sketch Totems (saved by Fritzing 0.9.2b)
breadboards: 1

parts:
  Parte1 = Arduino Uno (Rev3)
  LED1 = LED - 5mm [color="Red (633nm)" package="5 mm [THT]"]
  LED2 = LED - 5mm [color="Red (633nm)" package="5 mm [THT]"]
  S1 = Pushbutton [package="[THT]"]
  S2 = Pushbutton [package="[THT]"]
  S3 = Pushbutton [package="[THT]"]
  S4 = Pushbutton [package="[THT]"]
  S5 = Pushbutton [package="[THT]"]
  S6 = Pushbutton [package="[THT]"]
  R1 = Resistor [tolerance=±5% resistance=220 package=THT]
  R2 = Resistor [tolerance=±5% resistance=220 package=THT]
  R3 = Resistor [tolerance=±5% resistance=220 package=THT]
  R4 = Resistor [tolerance=±5% resistance=220 package=THT]
  R5 = Resistor [tolerance=±5% resistance=220 package=THT]
  R6 = Resistor [tolerance=±5% resistance=220 package=THT]

nets:
  N1: Parte1.D8, S6.Pin_1, S6.Pin_2, R6.Pin_1
  N2: Parte1.D13/SCK, LED1.cathode
  N3: Parte1.GND, LED1.anode, LED2.anode, R1.Pin_0, R2.Pin_0, R3.Pin_0, R4.Pin_0, R5.Pin_0, R6.Pin_0
  N4: Parte1.D2, LED2.cathode
  N5: Parte1.D3_PWM, S1.Pin_1, S1.Pin_2, R1.Pin_1
  N6: Parte1.D4, S2.Pin_1, S2.Pin_2, R2.Pin_1
  N7: Parte1.D5_PWM, S3.Pin_1, S3.Pin_2, R3.Pin_1
  N8: Parte1.D6_PWM, S4.Pin_1, S4.Pin_2, R4.Pin_1
  N9: Parte1.D7, S5.Pin_1, S5.Pin_2, R5.Pin_1
  N10: Parte1.5V, S1.Pin_3, S1.Pin_4, S2.Pin_3, S2.Pin_4, S3.Pin_3, S3.Pin_4, S5.Pin_3, S5.Pin_4, S6.Pin_3, S6.Pin_4
  N11: S4.Pin_3, S4.Pin_4
