# Fritzing sketch totems_con_solenoide (saved by Fritzing 0.9.2b)
breadboards: 1

parts:
  Parte1 = Arduino Uno (Rev3)
  U2 = HALL-EFFECT [package=sc70]
  U3 = HALL-EFFECT [package=sc70]
  U4 = HALL-EFFECT [package=sc70]
  U5 = HALL-EFFECT [package=sc70]
  U6 = HALL-EFFECT [package=sc70]
  U7 = HALL-EFFECT [package=sc70]
  LED1 = smd LED [color="Red (633nm)" package="0603 [SMD]"]
  LED2 = LED - 5mm [color="Green (570nm)" package="5 mm [THT]"]
  U8 = RELAY [package=relay-jzc]

nets:
  N1: Parte1.D9_PWM, LED2.cathode
  N2: Parte1.D10_PWM/SS, LED1.cathode
  N3: Parte1.D11_PWM/MOSI, U8.NO
  N4: Parte1.5V, U8.COIL2
  GND: Parte1.GND, U2.GND, U3.GND, U4.GND, U5.GND, U6.GND, U7.GND, LED1.anode, LED2.anode, U8.NC
