# Fritzing sketch cerradurade3anillos (saved by Fritzing 0.9.2b)
breadboards: 2

parts:
  Parte1 = Arduino Mega 2560 (Rev3)
  S1 = Pushbutton [package="[THT]"]
  S2 = Pushbutton [package="[THT]"]
  S3 = Pushbutton [package="[THT]"]
  S4 = Pushbutton [package="[THT]"]
  S5 = Pushbutton [package="[THT]"]
  S6 = Pushbutton [package="[THT]"]
  S7 = Pushbutton [package="[THT]"]
  S8 = Pushbutton [package="[THT]"]
  S9 = Pushbutton [package="[THT]"]
  S10 = Pushbutton [package="[THT]"]
  S11 = Pushbutton [package="[THT]"]
  S12 = Pushbutton [package="[THT]"]
  S13 = Pushbutton [package="[THT]"]
  S14 = Pushbutton [package="[THT]"]
  S15 = Pushbutton [package="[THT]"]
  S16 = Pushbutton [package="[THT]"]
  R1 = Resistor [tolerance=±5% resistance=220 package=THT]
  R2 = Resistor [tolerance=±5% resistance=220 package=THT]
  R3 = Resistor [tolerance=±5% resistance=220 package=THT]
  R4 = Resistor [tolerance=±5% resistance=220 package=THT]
  R5 = Resistor [tolerance=±5% resistance=220 package=THT]
  R6 = Resistor [tolerance=±5% resistance=220 package=THT]
  R7 = Resistor [tolerance=±5% resistance=220 package=THT]
  R8 = Resistor [tolerance=±5% resistance=220 package=THT]
  R9 = Resistor [tolerance=±5% resistance=220 package=THT]
  R10 = Resistor [tolerance=±5% resistance=220 package=THT]
  R11 = Resistor [tolerance=±5% resistance=220 package=THT]
  R12 = Resistor [tolerance=±5% resistance=220 package=THT]
  R13 = Resistor [tolerance=±5% resistance=220 package=THT]
  R14 = Resistor [tolerance=±5% resistance=220 package=THT]
  R15 = Resistor [tolerance=±5% resistance=220 package=THT]
  R16 = Resistor [tolerance=±5% resistance=220 package=THT]
  LED1 = LED - 5mm [color="Red (633nm)" package="5 mm [THT]"]
  LED2 = LED - 5mm [color="Red (633nm)" package="5 mm [THT]"]
  S17 = Pushbutton [package="[THT]"]
  S18 = Pushbutton [package="[THT]"]
  S19 = Pushbutton [package="[THT]"]
  S20 = Pushbutton [package="[THT]"]
  R17 = Resistor [tolerance=±5% resistance=220 package=THT]
  R18 = Resistor [tolerance=±5% resistance=220 package=THT]
  R19 = Resistor [tolerance=±5% resistance=220 package=THT]
  R20 = Resistor [tolerance=±5% resistance=220 package=THT]

nets:
  N1: Parte1.A8, S17.Pin_1, S17.Pin_2, R20.Pin_1
  N2: Parte1.A9, S18.Pin_1, S18.Pin_2, R19.Pin_1
  N3: Parte1.A0, S11.Pin_1, S11.Pin_2, R11.Pin_1
  N4: Parte1.A1, S12.Pin_1, S12.Pin_2, R15.Pin_1
  N5: Parte1.A2, S13.Pin_1, S13.Pin_2, R14.Pin_1
  N6: Parte1.A3, S14.Pin_1, S14.Pin_2, R13.Pin_1
  N7: Parte1.A4, S15.Pin_1, S15.Pin_2, R16.Pin_1
  N8: Parte1.A5, S16.Pin_1, S16.Pin_2, R3.Pin_0
  N9: Parte1.A6, S19.Pin_1, S19.Pin_2, R18.Pin_1
  N10: Parte1.A7, S20.Pin_1, S20.Pin_2, R17.Pin_1
  N11: Parte1.GND, R1.Pin_0, R2.Pin_0, R3.Pin_1, R4.Pin_0, R5.Pin_0, R6.Pin_0, R7.Pin_0, R8.Pin_0, R9.Pin_0, R10.Pin_0, R11.Pin_0, R12.Pin_0, R13.Pin_0, R14.Pin_0, R15.Pin_0, R16.Pin_0, LED1.anode, LED2.anode, R17.Pin_0, R18.Pin_0, R19.Pin_0, R20.Pin_0
  N12: Parte1.D13_PWM, LED2.cathode
  N13: Parte1.D12_PWM, S10.Pin_1, S10.Pin_2, R10.Pin_1
  N14: Parte1.D11_PWM, S9.Pin_1, S9.Pin_2, R9.Pin_1
  N15: Parte1.D10_PWM, S8.Pin_1, S8.Pin_2, R12.Pin_1
  N16: Parte1.D9_PWM, S7.Pin_1, S7.Pin_2, R5.Pin_1
  N17: Parte1.D8_PWM, S6.Pin_1, S6.Pin_2, R6.Pin_1
  N18: Parte1.5V, S1.Pin_3, S1.Pin_4, S2.Pin_3, S2.Pin_4, S3.Pin_3, S3.Pin_4, S4.Pin_3, S4.Pin_4, S5.Pin_3, S5.Pin_4, S6.Pin_3, S6.Pin_4, S7.Pin_3, S7.Pin_4, S8.Pin_3, S8.Pin_4, S9.Pin_3, S9.Pin_4, S10.Pin_3, S10.Pin_4, S11.Pin_3, S11.Pin_4, S12.Pin_3, S12.Pin_4, S13.Pin_3, S13.Pin_4, S14.Pin_3, S14.Pin_4, S15.Pin_3, S15.Pin_4, S16.Pin_3, S16.Pin_4, S17.Pin_3, S17.Pin_4, S18.Pin_3, S18.Pin_4, S19.Pin_3, S19.Pin_4, S20.Pin_3, S20.Pin_4
  N19: Parte1.D2_PWM, LED1.cathode
  N20: Parte1.D3_PWM, S1.Pin_1, S1.Pin_2, R4.Pin_1
  N21: Parte1.D4_PWM, S2.Pin_1, S2.Pin_2, R2.Pin_1
  N22: Parte1.D5_PWM, S3.Pin_1, S3.Pin_2, R1.Pin_1
  N23: Parte1.D6_PWM, S4.Pin_1, S4.Pin_2, R8.Pin_1
  N24: Parte1.D7_PWM, S5.Pin_1, S5.Pin_2, R7.Pin_1
