# Fritzing sketch secuenciaColores (saved by Fritzing 0.9.2b)
breadboards: 1

parts:
  Parte1 = Arduino Uno (Rev3)
  S6 = Pushbutton [package="[THT]"]
  R1 = Resistor [tolerance=±5% resistance=220 package=THT]
  S7 = Pushbutton [package="[THT]"]
  S8 = Pushbutton [package="[THT]"]
  S9 = Pushbutton [package="[THT]"]
  S10 = Pushbutton [package="[THT]"]
  S11 = Pushbutton [package="[THT]"]
  S12 = Pushbutton [package="[THT]"]
  R2 = Resistor [tolerance=±5% resistance=220 package=THT]
  R3 = Resistor [tolerance=±5% resistance=220 package=THT]
  R4 = Resistor [tolerance=±5% resistance=220 package=THT]
  R5 = Resistor [tolerance=±5% resistance=220 package=THT]
  R6 = Resistor [tolerance=±5% resistance=220 package=THT]
  R7 = Resistor [tolerance=±5% resistance=220 package=THT]
  LED1 = smd LED [color="Red (633nm)" package="0805 [SMD]"]
  LED2 = smd LED [color="Red (633nm)" package="0805 [SMD]"]
  LED3 = smd LED [color="Red (633nm)" package="0805 [SMD]"]
  LED4 = smd LED [color="Red (633nm)" package="0805 [SMD]"]
  LED5 = smd LED [color="Red (633nm)" package="0805 [SMD]"]
  LED6 = smd LED [color="Red (633nm)" package="0805 [SMD]"]
  LED7 = smd LED [color="Red (633nm)" package="0805 [SMD]"]

nets:
  N1: Parte1.D8, LED6.anode
  N2: Parte1.D9_PWM, LED5.anode
  N3: Parte1.D10_PWM/SS, LED4.anode
  N4: Parte1.D11_PWM/MOSI, LED3.anode
  N5: Parte1.D12/MISO, LED2.anode
  N6: Parte1.D13/SCK, LED1.anode
  N7: Parte1.D0/RX, S6.Pin_1, S6.Pin_2, R1.Pin_0
  N8: Parte1.D1/TX, S7.Pin_1, S7.Pin_2, R2.Pin_0
  N9: Parte1.D2, S8.Pin_1, S8.Pin_2, R6.Pin_0
  N10: Parte1.D3_PWM, S9.Pin_1, S9.Pin_2, R5.Pin_0
  N11: Parte1.D4, S10.Pin_1, S10.Pin_2, R4.Pin_0
  N12: Parte1.D5_PWM, S11.Pin_1, S11.Pin_2, R3.Pin_0
  N13: Parte1.D6_PWM, S12.Pin_1, S12.Pin_2, R7.Pin_0
  N14: Parte1.D7, LED7.anode
  N15: S6.Pin_3, S6.Pin_4, S7.Pin_3, S7.Pin_4, S8.Pin_3, S8.Pin_4, S9.Pin_3, S9.Pin_4, S10.Pin_3, S10.Pin_4, S11.Pin_3, S11.Pin_4, S12.Pin_3, S12.Pin_4
  N16: R1.Pin_1, R2.Pin_1, R3.Pin_1, R4.Pin_1, R5.Pin_1, R6.Pin_1, R7.Pin_1, LED1.cathode, LED2.cathode, LED3.cathode, LED4.cathode, LED5.cathode, LED6.cathode, LED7.cathode
