# Fritzing sketch tanquedecombustible (saved by Fritzing 0.9.2b)
breadboards: 1

parts:
  Parte1 = Arduino Uno (Rev3)
  LED1 = LED - 5mm [color="Red (633nm)" package="5 mm [THT]"]
  S1 = Pushbutton [package="[THT]"]
  S2 = Pushbutton [package="[THT]"]
  R1 = Resistor [tolerance=±5% resistance=220 package=THT]
  R2 = Resistor [tolerance=±5% resistance=220 package=THT]
  LED2 = LED - 5mm [color="Red (633nm)" package="5 mm [THT]"]

nets:
  N1: Parte1.D13/SCK, LED1.cathode
  N2: Parte1.GND, LED1.anode, R1.Pin_0, R2.Pin_0, LED2.anode
  N3: Parte1.D2, LED2.cathode
  N4: Parte1.D3_PWM, S1.Pin_1, S1.Pin_2, R2.Pin_1
  N5: Parte1.D4, S2.Pin_1, S2.Pin_2, R1.Pin_1
  N6: Parte1.5V, S1.Pin_3, S1.Pin_4, S2.Pin_3, S2.Pin_4
